# Fritzing sketch arduinoESC (saved by Fritzing 0.9.3b)
breadboards: 1

parts:
  texas_instruments = Arduino Uno (Rev3) - ICSP
  S1 = Pushbutton [package="[SMD]"]
  10K = 10K Ω Resistor [package="1206 [SMD]"]
  IC1 = LM2907 [package=THT]  # not connected

nets:
  N1: texas_instruments.GND, 10K.Pin_1
  N2: texas_instruments.D2, S1.Pin_1, S1.Pin_2, 10K.Pin_0
  N3: texas_instruments.5V, S1.Pin_3, S1.Pin_4

custom parts:
  10K Ω Resistor: A generic resistor
  LM2907: Texas Instruments Demodulator
